# Fritzing sketch smartie _sorter_3000 (saved by Fritzing 1.0.2b)
breadboards: 2

parts:
  Arduino_Nano = Arduino Nano (Rev3.0)
  2N2222 = NPN-Transistor [package="TO92 [THT]"]
  S1 = Round Pushbutton
  S2 = Round Pushbutton
  S3 = Round Pushbutton
  Power_switch = SWITCH-SPST-2 [package=switch-spst-vertical]
  R1 = Resistor [tolerance=±5% power=0.25W resistance=220 package=THT]
  R2 = Resistor [tolerance=±5% power=0.25W resistance=220 package=THT]
  R3 = Resistor [tolerance=±5% power=0.25W resistance=220 package=THT]
  VCC1 = Battery block 9V
  LED1 = LED - 3mm [color="White (6500K)" current=0.030A package="3 mm [THT]"]
  LED2 = LED - 3mm [color="White (6500K)" current=0.030A package="3 mm [THT]"]
  LED4 = LED - 3mm [color="White (6500K)" current=0.030A package="3 mm [THT]"]
  LED5 = LED - 3mm [color="White (6500K)" current=0.030A package="3 mm [THT]"]
  LED6 = LED - 3mm [color="White (6500K)" current=0.030A package="3 mm [THT]"]
  R4 = Resistor [tolerance=±5% power=0.25W resistance=220 package=THT]
  LED3 = LED - 3mm [color="White (6500K)" current=0.030A package="3 mm [THT]"]
  VCC3 = Battery
  VCC2 = Battery block 9V

nets:
  N1: Arduino_Nano.GND, 2N2222.E, R1.Pin_1, R2.Pin_1, R3.Pin_1, VCC1.-, VCC2.-
  N2: Arduino_Nano.D2, R4.Pin_1
  N3: Arduino_Nano.D3, S1.leg1, R1.Pin_0
  N4: Arduino_Nano.D4, S2.leg1, R2.Pin_0
  N5: Arduino_Nano.D5, S3.leg1, R3.Pin_0
  N6: Arduino_Nano.VIN, Power_switch.P
  N7: Arduino_Nano.5V, S1.leg0, S2.leg0, S3.leg0
  N8: 2N2222.B, R4.Pin_0
  N9: 2N2222.C, LED1.cathode, LED2.cathode, LED4.cathode, LED5.cathode, LED6.cathode, LED3.cathode
  N10: Power_switch.O, VCC1.+
  N11: LED1.anode, LED2.anode, LED4.anode, LED5.anode, LED6.anode, LED3.anode, VCC3.+
  N12: VCC3.-, VCC2.+
